# Fritzing sketch robot (saved by Fritzing 0.9.6b)
circuit board: 5cm x 5cm
circuit board: 5.5cm x 24cm
breadboards: 1

parts:
  HC-SR04 = mystery part, 4 pins [chip_label=?]
  PS2_Receiver = mystery part, 6 pins [chip_label=?]
  JDY-31_DIP = mystery part, 5 pins [chip_label=?]
  C1 = Ceramic Capacitor [capacitance=100nF voltage=35V package="200 mil [THT, multilayer]"]
  C2 = Ceramic Capacitor [capacitance=100nF voltage=35V package="200 mil [THT, multilayer]"]
  Buzzer = mystery part, 5 pins [chip_label=?]
  GY-BNO055 = mystery part, 8 pins [chip_label=?]
  Motor_Driver = Adafruit TB6612 DC and Stepper Motor Driver [part_number=TB6612]
  U1 = Raspberry Pi Pico
  TBL = KF301-2 [part_number=KF301-2 package="screwterminal-5mm 2 position"]
  TBR = KF301-2 [part_number=KF301-2 package="screwterminal-5mm 2 position"]
  R1 = Resistor [tolerance=±5% power=0.25 resistance=10k package=THT]
  R2 = Resistor [tolerance=±5% resistance=20k package=THT]

nets:
  N1: HC-SR04.pin1, U1.pin_40
  N2: HC-SR04.pin2, U1.pin_16
  N3: HC-SR04.pin3, R1.Pin_0, R2.Pin_1
  GND: HC-SR04.pin4, PS2_Receiver.pin3, JDY-31_DIP.pin5, Buzzer.pin1, GY-BNO055.pin2, Motor_Driver.GND#7, Motor_Driver.GND#20, Motor_Driver.GND#21, U1.pin_3, U1.pin_8, U1.pin_23, R2.Pin_0
  N4: PS2_Receiver.pin1, U1.pin_34
  N5: PS2_Receiver.pin2, U1.pin_32
  N6: PS2_Receiver.pin4, JDY-31_DIP.pin4, GY-BNO055.pin1, Motor_Driver.VCC, U1.pin_36
  N7: PS2_Receiver.pin5, U1.pin_31
  N8: PS2_Receiver.pin6, U1.pin_29
  N9: JDY-31_DIP.pin2, U1.pin_2
  N10: JDY-31_DIP.pin3, U1.pin_1
  N11: C1.0, Motor_Driver.MOTORB2, TBL.1
  N12: C1.1, Motor_Driver.MOTORB1, TBL.2
  N13: C2.0, Motor_Driver.MOTORA2, TBR.2
  N14: C2.1, Motor_Driver.MOTORA1, TBR.1
  N15: Buzzer.pin2, Buzzer.pin3, Buzzer.pin4, Buzzer.pin5, U1.pin_12
  N16: GY-BNO055.pin3, U1.pin_20
  N17: GY-BNO055.pin4, U1.pin_19
  N18: Motor_Driver.PWMB, U1.pin_27
  N19: Motor_Driver.BIN2, U1.pin_26
  N20: Motor_Driver.BIN1, U1.pin_25
  N21: Motor_Driver.AIN1, U1.pin_24
  N22: Motor_Driver.AIN2, U1.pin_22
  N23: Motor_Driver.PWMA, U1.pin_21
  N24: U1.pin_17, R1.Pin_1

notes:
  eigenein/robot 2020-04-23

custom parts:
  Adafruit TB6612 DC and Stepper Motor Driver: Spin two DC motors, step one bi-polar or uni-polar stepper, or fire off two solenoids with 1.2A per channel using the TB6612. These are perhaps better known as "the drivers in our assembled Adafruit Motorshield or Motor HAT." We really like these dual H-bridges, so if you want to control motors without a shield or HAT these are easy to include on any solderless breadboard or perma-proto.
  Raspberry Pi Pico: Raspberry Pi Pico. Based around the RP2040 microcontroller the Pico is a low cost microcontroller device bringing Raspberry Pi quality, cost, and easy of use to the microcontroller space. Jan 2021, Split part in to two versions: tht (this one) and SMD. This one will drill holes for a .1 in header in pcb to allow plugging in the module as well as providing pads to solder the module to the top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
  KF301-2: KF301-3 is a 3 position screw terminal header block with male through hole PCB pins on 5mm spacing
